# Fritzing sketch Publisher-Diagram (saved by Fritzing 0.9.3b)
breadboards: 1

parts:
  Raspberry_Pi1 = Raspberry Pi Zero
  R1 = Resistor [tolerance=±5% resistance=4.7k package=THT]
  DS1 = DS18B20 1-Wire Temperature Sensor [part_number=DS18B20]

nets:
  3V3: Raspberry_Pi1.3v3, R1.Pin_1, DS1.VDD
  N1: Raspberry_Pi1.GIPO4, R1.Pin_0, DS1.DQ
  GND: Raspberry_Pi1.GND, DS1.GND

notes:
  The 4.7k Ohm resistor connects the VCC pin of the DS18B20 to the output (middle) pin. This ensure that the pin is pulled high.

custom parts:
  Raspberry Pi Zero: The Raspberry Pi Zero is the latest single board computer to be released by the Raspberry Pi Foundation. It is the entry level model Raspberry Pi perfect for hobbyists, makers and industrial engineers looking to create solutions where small size and low power consumption are important. This is especially relevant for applications in the wearables space as well as up and coming applications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
